// Logisim project COSC201_HW03_JF.circ as structural Verilog: 4 circuits, main circuit XOR
module XOR (
  input  A,
  input  B,
  output A_XOR_B
);

  wire transistor_1_out, transistor_2_out, transistor_3_out, transistor_8_out, transistor_9_out,
       transistor_11_out, transistor_13_out;

  Transistor #(.\type ("n")) transistor_1 (.in(1'b0), .out(transistor_1_out), .gate(B));
  Transistor transistor_2 (.in(1'b1), .out(transistor_2_out), .gate(A));
  Transistor transistor_3 (.in(1'b1), .out(transistor_3_out), .gate(A));
  Transistor transistor_4 (.in(transistor_3_out), .out(transistor_1_out), .gate(B));
  Transistor #(.\type ("n")) transistor_5 (.in(1'b0), .out(transistor_1_out), .gate(A));
  Transistor transistor_6 (.in(1'b1), .out(transistor_2_out), .gate(B));
  Transistor #(.\type ("n")) transistor_7 (.in(transistor_8_out), .out(transistor_2_out), .gate(B));
  Transistor #(.\type ("n")) transistor_8 (.in(1'b0), .out(transistor_8_out), .gate(A));
  Transistor transistor_9 (.in(1'b1), .out(transistor_9_out), .gate(transistor_1_out));
  Transistor #(.\type ("n")) transistor_10 (.in(1'b0), .out(transistor_9_out), .gate(transistor_1_out));
  Transistor transistor_11 (.in(1'b1), .out(transistor_11_out), .gate(transistor_9_out));
  Transistor #(.\type ("n")) transistor_12 (.in(transistor_13_out), .out(transistor_11_out), .gate(transistor_9_out));
  Transistor #(.\type ("n")) transistor_13 (.in(1'b0), .out(transistor_13_out), .gate(transistor_2_out));
  Transistor transistor_14 (.in(1'b1), .out(transistor_11_out), .gate(transistor_2_out));
  Transistor transistor_15 (.in(1'b1), .out(A_XOR_B), .gate(transistor_11_out));
  Transistor #(.\type ("n")) transistor_16 (.in(1'b0), .out(A_XOR_B), .gate(transistor_11_out));
endmodule

module Switch (
  input  S,
  input  A,
  input  B,
  output C,
  output D
);

  wire and_1_out, and_2_out, and_3_out, and_4_out;

  and and_1 (and_1_out, ~S, A);  // AND_Gate
  and and_2 (and_2_out, S, B);
  and and_3 (and_3_out, ~S, B);  // AND_Gate
  and and_4 (and_4_out, S, A);
  or or_1 (C, and_1_out, and_2_out);
  or or_2 (D, and_3_out, and_4_out);
endmodule

module Arith (
  input  [7:0] A,
  input  [7:0] B,
  input  [1:0] Opcode,
  output [7:0] Result
);

  wire [7:0] multiplexer_1_out, multiplexer_2_out, not_1_out;

  Multiplexer #(.width(8), .enable("false")) multiplexer_1 (
    .in0(8'h1), .in1(B), .out(multiplexer_1_out), .sel(Opcode[1]));
  assign not_1_out = ~multiplexer_1_out;  // NOT_Gate not_1, 8 bits wide
  Multiplexer #(.width(8), .enable("false")) multiplexer_2 (
    .in0(not_1_out), .in1(multiplexer_1_out), .out(multiplexer_2_out), .sel(Opcode[0]));
  Adder adder_1 (.a(A), .b(multiplexer_2_out), .out(Result));  // open: cin, cout
endmodule

module two_bit_adder (
  input  a,
  input  b,
  input  c,
  input  d,
  output x,
  output y,
  output z
);

  wire and_1_out, and_2_out, and_3_out, and_4_out, and_5_out, and_6_out, and_7_out, and_8_out, and_9_out,
       and_10_out, and_11_out, and_12_out, not_1_out, not_2_out, not_3_out, not_4_out, not_5_out, not_6_out,
       not_7_out, not_8_out, not_9_out, not_10_out, not_11_out, not_12_out;

  not not_1 (not_1_out, a);
  not not_2 (not_2_out, b);
  not not_3 (not_3_out, a);
  not not_4 (not_4_out, d);
  not not_5 (not_5_out, a);
  not not_6 (not_6_out, c);
  not not_7 (not_7_out, b);
  not not_8 (not_8_out, c);
  not not_9 (not_9_out, c);
  not not_10 (not_10_out, d);
  not not_11 (not_11_out, b);
  and and_1 (and_1_out, not_11_out, d);
  and and_2 (and_2_out, b, not_12_out);
  not not_12 (not_12_out, d);
  and and_3 (and_3_out, a, b, c);
  and and_4 (and_4_out, b, c, d);
  and and_5 (and_5_out, a, c);
  and and_6 (and_6_out, a, b, d);
  and and_7 (and_7_out, not_1_out, not_2_out, c);
  and and_8 (and_8_out, not_3_out, c, not_4_out);
  and and_9 (and_9_out, not_5_out, b, not_6_out, d);
  and and_10 (and_10_out, a, not_7_out, not_8_out);
  and and_11 (and_11_out, a, not_9_out, not_10_out);
  and and_12 (and_12_out, a, b, c, d);
  or or_1 (y, and_1_out, and_2_out, and_3_out);
  or or_2 (z, and_4_out, and_5_out, and_6_out);
  or or_3 (x, and_7_out, and_8_out, and_9_out, and_10_out, and_11_out, and_12_out);
endmodule
