// Logisim project adderJF.circ as structural Verilog: 4 circuits, main circuit main
module main (
  input  Ci,
  input  [31:0] A,
  input  [31:0] B,
  output [31:0] S,
  output Co,
  output [31:0] S_2,
  output Co_2
);

  Adder #(.width(32)) adder_1 (.a(A), .b(B), .out(S), .cin(Ci), .cout(Co));
  add32 add32_1 (.A(A), .B(B), .Ci(Ci), .Co(Co_2), .S(S_2));

  // Notes on the sheet:
  //   Jonah Fidel 
  //   10/5/14
endmodule

module add1 (
  input  Ci,
  input  A,
  input  B,
  output S,
  output Co
);

  wire and_1_out, and_2_out, xor_1_out;

  xor xor_1 (xor_1_out, A, B);
  and and_1 (and_1_out, B, A);
  xor xor_2 (S, xor_1_out, Ci);
  and and_2 (and_2_out, xor_1_out, Ci);
  or or_1 (Co, and_2_out, and_1_out);
endmodule

module add8 (
  input  Ci,
  input  [7:0] A,
  input  [7:0] B,
  output [7:0] S,
  output Co
);

  wire add1_1_co, add1_2_co, add1_3_co, add1_4_co, add1_5_co, add1_6_co, add1_7_co;

  add1 add1_1 (.A(A[0]), .B(B[0]), .Ci(Ci), .Co(add1_1_co), .S(S[0]));
  add1 add1_2 (.A(A[1]), .B(B[1]), .Ci(add1_1_co), .Co(add1_2_co), .S(S[1]));
  add1 add1_3 (.A(A[2]), .B(B[2]), .Ci(add1_2_co), .Co(add1_3_co), .S(S[2]));
  add1 add1_4 (.A(A[3]), .B(B[3]), .Ci(add1_3_co), .Co(add1_4_co), .S(S[3]));
  add1 add1_5 (.A(A[4]), .B(B[4]), .Ci(add1_4_co), .Co(add1_5_co), .S(S[4]));
  add1 add1_6 (.A(A[5]), .B(B[5]), .Ci(add1_5_co), .Co(add1_6_co), .S(S[5]));
  add1 add1_7 (.A(A[6]), .B(B[6]), .Ci(add1_6_co), .Co(add1_7_co), .S(S[6]));
  add1 add1_8 (.A(A[7]), .B(B[7]), .Ci(add1_7_co), .Co(Co), .S(S[7]));

  // Notes on the sheet:
  //   Add 8-bit numbers by combining eight 1-bit adders.
endmodule

module add32 (
  input  Ci,
  input  [31:0] A,
  input  [31:0] B,
  output [31:0] S,
  output Co
);

  wire add8_1_co, add8_2_co, add8_3_co;

  add8 add8_1 (.A(A[7:0]), .B(B[7:0]), .Ci(Ci), .Co(add8_1_co), .S(S[7:0]));
  add8 add8_2 (.A(A[15:8]), .B(B[15:8]), .Ci(add8_1_co), .Co(add8_2_co), .S(S[15:8]));
  add8 add8_3 (.A(A[23:16]), .B(B[23:16]), .Ci(add8_2_co), .Co(add8_3_co), .S(S[23:16]));
  add8 add8_4 (.A(A[31:24]), .B(B[31:24]), .Ci(add8_3_co), .Co(Co), .S(S[31:24]));

  // Notes on the sheet:
  //   Add 32-bit numbers by combining four 8-bit adders.
endmodule
