// Logisim project shifter8x4JF.circ as structural Verilog: 2 circuits, main circuit main
module main (
  input  [7:0] in_1,
  input  [1:0] in_2,
  output [7:0] out_3
);

  shifter8x4 shifter8x4_1 (.Input(in_1), .Control(in_2), .Output(out_3));
endmodule

module shifter8x4 (
  input  [7:0] Input,
  input  [1:0] Control,
  output [7:0] Output
);

  wire [0:0] undriven;

  Multiplexer #(.select(2), .width(8), .enable("false")) multiplexer_1 (
    .in0(Input), .in1({Input[6:0], undriven[0]}), .in2({Input[5:0], 2'b00}), .in3({Input[4:0], 3'b000}),
    .out(Output), .sel(Control));
endmodule
