// Logisim project SingleCycleCPU.circ as structural Verilog: 1 circuit, main circuit Datapath
module Datapath (
  input  [9:0] in_1,
  input  Reset,
  input  [3:0] in_3,
  input  Clear_Data_Mem,
  input  Clear_Instr_Mem
);

  wire ALU_zero, and_1_out, Clock_out, Control_alusrc, Control_branch, Control_jump, Control_memread,
       Control_memtoreg, Control_memwrite, Control_regdest, Control_regwrite;
  wire [1:0] Control_aluop, data_mem_interface_1_mem_control;
  wire [3:0] ALU_Control_operation;
  wire [4:0] instructiondecode_1_rd, instructiondecode_1_rs, instructiondecode_1_rt, multiplexer_1_out;
  wire [5:0] instructiondecode_1_funct, instructiondecode_1_op;
  wire [7:0] data_mem_interface_1_address_to_mem, Instr_Mem_to_inst_mem;
  wire [15:0] instructiondecode_1_immediate;
  wire [25:0] instructiondecode_1_address;
  wire [31:0] adder_1_out, ALU_result, branchaddress_1_branchaddress, data_mem_interface_1_data_from_mem,
       data_mem_interface_1_data_from_memory, Extend_out_2, Instr_Mem_instruction, jumpaddress_1_jumpaddress,
       multiplexer_2_out, multiplexer_3_out, multiplexer_4_out, multiplexer_5_out, PC_q, ram_1_data,
       Register_file_readdata1, Register_file_readdata2;

  Register #(.width(32)) PC (.D(multiplexer_4_out), .Q(PC_q), .clk(Clock_out), .clr(Reset));  // open: en
  Clock Clock (.out(Clock_out));
  Inst_Mem_Interface Instr_Mem (
    .Instruction_Address(PC_q), .To_Inst_Mem(Instr_Mem_to_inst_mem), .Mem_To_Interface(ram_1_data),
    .Instruction(Instr_Mem_instruction));
  Adder #(.width(32)) adder_1 (.a(32'h4), .b(PC_q), .out(adder_1_out));  // open: cin, cout
  JumpAddress jumpaddress_1 (
    .PC_4(adder_1_out), .Address(instructiondecode_1_address), .JumpAddress(jumpaddress_1_jumpaddress));
  InstructionDecode instructiondecode_1 (
    .Instruction(Instr_Mem_instruction), .address(instructiondecode_1_address), .op(instructiondecode_1_op),
    .rs(instructiondecode_1_rs), .rt(instructiondecode_1_rt), .rd(instructiondecode_1_rd),
    .immediate(instructiondecode_1_immediate), .funct(instructiondecode_1_funct));  // open: shamt
  RAM #(.dataWidth(32)) ram_1 (
    .addr(Instr_Mem_to_inst_mem), .data(ram_1_data), .sel(1'b1), .clk(1'b0), .ld(1'b1), .clr(Clear_Instr_Mem));
  Fake_Control Control (
    .op(instructiondecode_1_op), .test(in_1), .Branch(Control_branch), .Jump(Control_jump),
    .MemToReg(Control_memtoreg), .MemRead(Control_memread), .MemWrite(Control_memwrite),
    .ALUsrc(Control_alusrc), .ALUop(Control_aluop), .RegWrite(Control_regwrite), .RegDest(Control_regdest));
  Multiplexer #(.width(5)) multiplexer_1 (
    .in0(instructiondecode_1_rt), .in1(instructiondecode_1_rd), .out(multiplexer_1_out), .sel(Control_regdest));  // open: en
  SignExtend Extend (.in_1(instructiondecode_1_immediate), .out_2(Extend_out_2));
  Registers Register_file (
    .ReadRegister1(instructiondecode_1_rs), .ReadRegister2(instructiondecode_1_rt),
    .WriteRegister(multiplexer_1_out), .WriteData(multiplexer_5_out), .Write(Control_regwrite),
    .Clock(Clock_out), .Clear(Reset), .ReadData1(Register_file_readdata1), .ReadData2(Register_file_readdata2));
  Multiplexer #(.width(32)) multiplexer_2 (
    .in0(Register_file_readdata2), .in1(Extend_out_2), .out(multiplexer_2_out), .sel(Control_alusrc));  // open: en
  Fake_ALUcontrol ALU_Control (
    .ALUop(Control_aluop), .funct(instructiondecode_1_funct), .test(in_3), .Operation(ALU_Control_operation));
  BranchAddress branchaddress_1 (
    .PC_4(adder_1_out), .Address(Extend_out_2), .BranchAddress(branchaddress_1_branchaddress));
  ALU ALU (
    .A(Register_file_readdata1), .B(multiplexer_2_out), .Operation(ALU_Control_operation), .Zero(ALU_zero),
    .Result(ALU_result));  // open: Overflow
  Multiplexer #(.width(32)) multiplexer_3 (
    .in0(adder_1_out), .in1(branchaddress_1_branchaddress), .out(multiplexer_3_out), .sel(and_1_out));  // open: en
  and and_1 (and_1_out, Control_branch, ALU_zero);
  Multiplexer #(.width(32)) multiplexer_4 (
    .in0(jumpaddress_1_jumpaddress), .in1(multiplexer_3_out), .out(multiplexer_4_out), .sel(Control_jump));  // open: en
  Data_Mem_Interface data_mem_interface_1 (
    .Data_Address(ALU_result), .Data_to_Memory(ALU_result), .MemWrite(Control_memwrite),
    .MemRead(Control_memread), .Clock___Rising_Edge(Clock_out),
    .Address_To_Mem(data_mem_interface_1_address_to_mem), .Mem_Control(data_mem_interface_1_mem_control),
    .Data_To_Mem(data_mem_interface_1_data_from_mem), .Data_From_Mem(data_mem_interface_1_data_from_mem),
    .Data_from_Memory(data_mem_interface_1_data_from_memory));
  RAM #(.dataWidth(32)) ram_2 (
    .addr(data_mem_interface_1_address_to_mem), .data(data_mem_interface_1_data_from_mem), .sel(1'b1),
    .clk(data_mem_interface_1_mem_control[0]), .ld(data_mem_interface_1_mem_control[1]), .clr(Clear_Data_Mem));
  Multiplexer #(.width(32)) multiplexer_5 (
    .in0(data_mem_interface_1_data_from_memory), .in1(ALU_result), .out(multiplexer_5_out),
    .sel(Control_memtoreg));  // open: en

  // Notes on the sheet:
  //   Jonah Fidel
  //   10/27/14
  //   Decode
endmodule
