// Logisim project PipelineCPU1-start.circ as structural Verilog: 1 circuit, main circuit Datapath
module Datapath (
  input  Reset,
  input  Clear_Data_Mem,
  input  Clear_Instr_Mem
);

  wire ALU_zero, and_1_out, Clock_out, Control_alusrc, Control_branch, Control_jump, Control_memread,
       Control_memtoreg, Control_memwrite, Control_regdest, Control_regwrite, PR2Ctrl_alusrc_out,
       PR2Ctrl_branch_out, PR2Ctrl_jump_out, PR2Ctrl_memread_out, PR2Ctrl_memtoreg_out, PR2Ctrl_memwrite_2,
       PR2Ctrl_regdest_out, PR2Ctrl_regwrite_out, PR3Ctrl_branch_out, PR3Ctrl_jump_out, PR3Ctrl_memread_out,
       PR3Ctrl_memtoreg_out, PR3Ctrl_memwrite_2, PR3Ctrl_regwrite_out, PR3DP_zero_2, PR4Ctrl_memtoregout,
       PR4Ctrl_regwriteout;
  wire [1:0] Control_aluop, data_mem_interface_1_mem_control, PR2Ctrl_aluop_out;
  wire [3:0] ALU_Control_operation;
  wire [4:0] Decode_rd, Decode_rs, Decode_rt, multiplexer_1_out, PR2FnReg_rd_out, PR2FnReg_rt_out,
       PR3_4R_2_out, PR3_4R_out;
  wire [5:0] Decode_funct, Decode_op, PR2FnReg_funct_out;
  wire [7:0] data_mem_interface_1_address_to_mem, I_Mem_to_inst_mem;
  wire [15:0] Decode_immediate;
  wire [25:0] Decode_address, PR2PC_jump_addr_out, PR3PC_jump_addr_out;
  wire [31:0] adder_1_out, ALU_result, BA_branchaddress, data_mem_interface_1_data_from_mem,
       data_mem_interface_1_data_from_memory, Extend_out_2, I_Mem_instruction, JA_jumpaddress,
       multiplexer_2_out, multiplexer_3_out, multiplexer_4_out, multiplexer_5_out, PC_q, PR1_ir_out,
       PR1_pc_4_out, PR2DP_a_reg, PR2DP_b_reg, PR2DP_sign_ext_immediate_2, PR2PC_pc_4_out,
       PR3DP_alu_result_out, PR3DP_b_reg, PR3PC_branch_address_out, PR4DP_aluoutout, PR4DP_readdataout,
       ram_1_data, Registers_readdata1, Registers_readdata2;

  Register #(.width(32)) PC (.D(multiplexer_4_out), .Q(PC_q), .clk(Clock_out), .clr(Reset));  // open: en
  Clock Clock (.out(Clock_out));
  Adder #(.width(32)) adder_1 (.a(32'h4), .b(PC_q), .out(adder_1_out));  // open: cin, cout
  Inst_Mem_Interface I_Mem (
    .Instruction_Address(PC_q), .To_Inst_Mem(I_Mem_to_inst_mem), .Mem_To_Interface(ram_1_data),
    .Instruction(I_Mem_instruction));
  PipeReg1 PR1 (
    .PC_4(adder_1_out), .Instruction(I_Mem_instruction), .Clock(Clock_out), .Reset(Reset),
    .PC_4_out(PR1_pc_4_out), .IR_out(PR1_ir_out));
  RAM #(.dataWidth(32)) ram_1 (
    .addr(I_Mem_to_inst_mem), .data(ram_1_data), .sel(1'b1), .clk(1'b0), .ld(1'b1), .clr(Clear_Instr_Mem));
  Control Control (
    .op(Decode_op), .Branch(Control_branch), .Jump(Control_jump), .MemToReg(Control_memtoreg),
    .MemRead(Control_memread), .MemWrite(Control_memwrite), .ALUsrc(Control_alusrc), .ALUop(Control_aluop),
    .RegWrite(Control_regwrite), .RegDest(Control_regdest));
  InstructionDecode Decode (
    .Instruction(PR1_ir_out), .address(Decode_address), .op(Decode_op), .rs(Decode_rs), .rt(Decode_rt),
    .rd(Decode_rd), .immediate(Decode_immediate), .funct(Decode_funct));  // open: shamt
  Registers Registers (
    .ReadRegister1(Decode_rs), .ReadRegister2(Decode_rt), .WriteRegister(PR3_4R_2_out),
    .WriteData(multiplexer_5_out), .Write(PR4Ctrl_regwriteout), .Clock(Clock_out), .Clear(Reset),
    .ReadData1(Registers_readdata1), .ReadData2(Registers_readdata2));
  PipeReg2PC PR2PC (
    .PC_4_in(PR1_pc_4_out), .Jump_Addr_in(Decode_address), .Clock(Clock_out), .Reset(Reset),
    .PC_4_out(PR2PC_pc_4_out), .Jump_Addr_out(PR2PC_jump_addr_out));
  PipeReg2Ctrl PR2Ctrl (
    .Branch(Control_branch), .Jump(Control_jump), .MemToReg(Control_memtoreg), .MemRead(Control_memread),
    .MemWrite(Control_memwrite), .ALUsrc(Control_alusrc), .ALUOp(Control_aluop), .RegWrite(Control_regwrite),
    .RegDest(Control_regdest), .Clock(Clock_out), .Reset(Reset), .Branch_out(PR2Ctrl_branch_out),
    .Jump_out(PR2Ctrl_jump_out), .MemToReg_out(PR2Ctrl_memtoreg_out), .MemRead_out(PR2Ctrl_memread_out),
    .MemWrite_2(PR2Ctrl_memwrite_2), .ALUsrc_out(PR2Ctrl_alusrc_out), .ALUOp_out(PR2Ctrl_aluop_out),
    .RegWrite_out(PR2Ctrl_regwrite_out), .RegDest_out(PR2Ctrl_regdest_out));
  PipeReg2DP PR2DP (
    .A_Register(Registers_readdata1), .B_Register(Registers_readdata2), .Sign_Ext_Immediate(Extend_out_2),
    .Clock(Clock_out), .Reset(Reset), .A_Reg(PR2DP_a_reg), .B_Reg(PR2DP_b_reg),
    .Sign_Ext_Immediate_2(PR2DP_sign_ext_immediate_2));
  SignExtend Extend (.in_1(Decode_immediate), .out_2(Extend_out_2));
  PipeReg2FnReg PR2FnReg (
    .Funct(Decode_funct), .Rt(Decode_rt), .Rd(Decode_rd), .Clock(Clock_out), .Reset(Reset),
    .Funct_out(PR2FnReg_funct_out), .Rt_out(PR2FnReg_rt_out), .Rd_out(PR2FnReg_rd_out));
  Multiplexer #(.width(5), .enable("false")) multiplexer_1 (
    .in0(PR2FnReg_rt_out), .in1(PR2FnReg_rd_out), .out(multiplexer_1_out), .sel(PR2Ctrl_regdest_out));
  BranchAddress BA (.PC_4(PR2PC_pc_4_out), .Address(Extend_out_2), .BranchAddress(BA_branchaddress));
  ALU ALU (
    .A(PR2DP_a_reg), .B(multiplexer_2_out), .Operation(ALU_Control_operation), .Zero(ALU_zero),
    .Result(ALU_result));  // open: Overflow
  Multiplexer #(.width(32), .enable("false")) multiplexer_2 (
    .in0(PR2DP_b_reg), .in1(PR2DP_sign_ext_immediate_2), .out(multiplexer_2_out), .sel(PR2Ctrl_alusrc_out));
  ALUcontrol ALU_Control (.ALUop(PR2Ctrl_aluop_out), .funct(PR2FnReg_funct_out), .Operation(ALU_Control_operation));
  PipeReg3PC PR3PC (
    .Branch_Address_in(BA_branchaddress), .Jump_Addr_in(PR2PC_jump_addr_out), .Clock(Clock_out),
    .Reset(Reset), .Branch_Address_out(PR3PC_branch_address_out), .Jump_Addr_out(PR3PC_jump_addr_out));
  PipeReg3Ctrl PR3Ctrl (
    .Branch(PR2Ctrl_branch_out), .Jump(PR2Ctrl_jump_out), .MemToReg(PR2Ctrl_memtoreg_out),
    .MemRead(PR2Ctrl_memread_out), .MemWrite(PR2Ctrl_memwrite_2), .RegWrite(PR2Ctrl_regwrite_out),
    .Clock(Clock_out), .Reset(Reset), .Branch_out(PR3Ctrl_branch_out), .Jump_out(PR3Ctrl_jump_out),
    .MemToReg_out(PR3Ctrl_memtoreg_out), .MemRead_out(PR3Ctrl_memread_out), .MemWrite_2(PR3Ctrl_memwrite_2),
    .RegWrite_out(PR3Ctrl_regwrite_out));
  PipeReg3DP PR3DP (
    .B_Register(PR2DP_b_reg), .B_Reg(PR3DP_b_reg), .ALU_Result_in(ALU_result),
    .AlU_result_out(PR3DP_alu_result_out), .Clock(Clock_out), .Reset(Reset), .zero(ALU_zero),
    .zero_2(PR3DP_zero_2));
  PipeReg3_4Reg PR3_4R (.in(multiplexer_1_out), .out(PR3_4R_out), .clock(Clock_out), .reset(Reset));
  JumpAddress JA (.PC_4(adder_1_out), .Address(PR3PC_jump_addr_out), .JumpAddress(JA_jumpaddress));
  Data_Mem_Interface data_mem_interface_1 (
    .Data_Address(PR3DP_alu_result_out), .Data_to_Memory(PR3DP_b_reg), .MemWrite(PR3Ctrl_memwrite_2),
    .MemRead(PR3Ctrl_memread_out), .Clock___Rising_Edge(Clock_out),
    .Address_To_Mem(data_mem_interface_1_address_to_mem), .Mem_Control(data_mem_interface_1_mem_control),
    .Data_To_Mem(data_mem_interface_1_data_from_mem), .Data_From_Mem(data_mem_interface_1_data_from_mem),
    .Data_from_Memory(data_mem_interface_1_data_from_memory));
  Multiplexer #(.width(32), .enable("false")) multiplexer_3 (
    .in0(adder_1_out), .in1(PR3PC_branch_address_out), .out(multiplexer_3_out), .sel(and_1_out));
  and and_1 (and_1_out, PR3Ctrl_branch_out, PR3DP_zero_2);
  PipeReg4DP PR4DP (
    .ReadDataIn(data_mem_interface_1_data_from_memory), .ReadDataOut(PR4DP_readdataout),
    .ALUOutIn(PR3DP_alu_result_out), .ALUOutOut(PR4DP_aluoutout), .Clock(Clock_out), .Reset(Reset));
  RAM #(.dataWidth(32)) ram_2 (
    .addr(data_mem_interface_1_address_to_mem), .data(data_mem_interface_1_data_from_mem), .sel(1'b1),
    .clk(data_mem_interface_1_mem_control[0]), .ld(data_mem_interface_1_mem_control[1]), .clr(Clear_Data_Mem));
  Multiplexer #(.width(32), .enable("false")) multiplexer_4 (
    .in0(multiplexer_3_out), .in1(JA_jumpaddress), .out(multiplexer_4_out), .sel(PR3Ctrl_jump_out));
  PipeReg4Ctrl PR4Ctrl (
    .RegWrite(PR3Ctrl_regwrite_out), .MemToReg(PR3Ctrl_memtoreg_out), .clock(Clock_out),
    .RegWriteOut(PR4Ctrl_regwriteout), .MemToRegOut(PR4Ctrl_memtoregout), .reset(Reset));
  PipeReg3_4Reg PR3_4R_2 (.in(PR3_4R_out), .out(PR3_4R_2_out), .clock(Clock_out), .reset(Reset));
  Multiplexer #(.width(32), .enable("false")) multiplexer_5 (
    .in0(PR4DP_aluoutout), .in1(PR4DP_readdataout), .out(multiplexer_5_out), .sel(PR4Ctrl_memtoregout));

  // Notes on the sheet:
  //   Your Name
  //   Today's Date
  //   EX/Mem
  //   BrOrPC
  //   JorPC
  //   Mem/WB
  //   MemToReg
endmodule
