// Logisim project pipelineRegisters-start.circ as structural Verilog: 11 circuits, main circuit PipeReg1
module PipeReg1 (
  input  [31:0] PC_4,
  input  [31:0] Instruction,
  input  Clock,
  input  Reset,
  output [31:0] PC_4_out,
  output [31:0] IR_out
);

  Register #(.width(32)) PC_4_Reg (.D(PC_4), .Q(PC_4_out), .clk(Clock), .clr(Reset));  // open: en
  Register #(.width(32)) IR (.D(Instruction), .Q(IR_out), .clk(Clock), .clr(Reset));  // open: en
endmodule

module PipeReg2DP (
  input  [31:0] A_Register,
  input  [31:0] B_Register,
  input  [31:0] Sign_Ext_Immediate,
  input  Clock,
  input  Reset,
  output [31:0] A_Reg,
  output [31:0] B_Reg,
  output [31:0] Sign_Ext_Immediate_2
);

  Register #(.width(32)) u_A_reg (.D(A_Register), .Q(A_Reg), .clk(Clock), .clr(Reset));  // open: en
  Register #(.width(32)) u_B_Reg (.D(B_Register), .Q(B_Reg), .clk(Clock), .clr(Reset));  // open: en
  Register #(.width(32)) Immediate_sign_extended (
    .D(Sign_Ext_Immediate), .Q(Sign_Ext_Immediate_2), .clk(Clock), .clr(Reset));  // open: en
endmodule

module PipeReg2FnReg (
  input  [5:0] Funct,
  input  [4:0] Rt,
  input  [4:0] Rd,
  input  Clock,
  input  Reset,
  output [5:0] Funct_out,
  output [4:0] Rt_out,
  output [4:0] Rd_out
);

  Register #(.width(6)) ALU_Control (.D(Funct), .Q(Funct_out), .clk(Clock), .clr(Reset));  // open: en
  Register #(.width(10)) Rt_Rd (.D({Rd, Rt}), .Q({Rd_out, Rt_out}), .clk(Clock), .clr(Reset));  // open: en
endmodule

module PipeReg2Ctrl (
  input  Branch,
  input  Jump,
  input  MemToReg,
  input  MemRead,
  input  MemWrite,
  input  ALUsrc,
  input  [1:0] ALUOp,
  input  RegWrite,
  input  RegDest,
  input  Clock,
  input  Reset,
  output Branch_out,
  output Jump_out,
  output MemToReg_out,
  output MemRead_out,
  output MemWrite_2,
  output ALUsrc_out,
  output [1:0] ALUOp_out,
  output RegWrite_out,
  output RegDest_out
);

  Register #(.width(10)) PipelineReg2c (
    .D({RegDest, RegWrite, ALUOp, ALUsrc, MemWrite, MemRead, MemToReg, Jump, Branch}),
    .Q({RegDest_out, RegWrite_out, ALUOp_out, ALUsrc_out, MemWrite_2, MemRead_out, MemToReg_out, Jump_out, Branch_out}),
    .clk(Clock), .clr(Reset));  // open: en
endmodule

module PipeReg2PC (
  input  [31:0] PC_4_in,
  input  [25:0] Jump_Addr_in,
  input  Clock,
  input  Reset,
  output [31:0] PC_4_out,
  output [25:0] Jump_Addr_out
);

  Register #(.width(32)) register_1 (.D(PC_4_in), .Q(PC_4_out), .clk(Clock), .clr(Reset));  // open: en
  Register #(.width(26)) register_2 (.D(Jump_Addr_in), .Q(Jump_Addr_out), .clk(Clock), .clr(Reset));  // open: en
endmodule

module PipeReg3PC (
  input  [31:0] Branch_Address_in,
  input  [25:0] Jump_Addr_in,
  input  Clock,
  input  Reset,
  output [31:0] Branch_Address_out,
  output [25:0] Jump_Addr_out
);

  Register #(.width(32)) register_1 (
    .D(Branch_Address_in), .Q(Branch_Address_out), .clk(Clock), .clr(Reset));  // open: en
  Register #(.width(26)) register_2 (.D(Jump_Addr_in), .Q(Jump_Addr_out), .clk(Clock), .clr(Reset));  // open: en
endmodule

module PipeReg3Ctrl (
  input  Branch,
  input  Jump,
  input  MemToReg,
  input  MemRead,
  input  MemWrite,
  input  RegWrite,
  input  Clock,
  input  Reset,
  output Branch_out,
  output Jump_out,
  output MemToReg_out,
  output MemRead_out,
  output MemWrite_2,
  output RegWrite_out
);

  Register #(.width(6)) PipelineReg2c (
    .D({RegWrite, MemWrite, MemRead, MemToReg, Jump, Branch}),
    .Q({RegWrite_out, MemWrite_2, MemRead_out, MemToReg_out, Jump_out, Branch_out}), .clk(Clock), .clr(Reset));  // open: en
endmodule

module PipeReg3DP (
  input  zero,
  input  [31:0] B_Register,
  input  [31:0] ALU_Result_in,
  input  Clock,
  input  Reset,
  output zero_2,
  output [31:0] B_Reg,
  output [31:0] AlU_result_out
);

  Register #(.width(1)) u_zero (.D(zero), .Q(zero_2), .clk(Clock), .clr(Reset));  // open: en
  Register #(.width(32)) u_B_Reg (.D(B_Register), .Q(B_Reg), .clk(Clock), .clr(Reset));  // open: en
  Register #(.width(32)) ALU_Result (.D(ALU_Result_in), .Q(AlU_result_out), .clk(Clock), .clr(Reset));  // open: en
endmodule

module PipeReg3_4Reg (
  input  [4:0] in,
  input  clock,
  input  reset,
  output [4:0] out
);

  wire [4:0] register_1_q;

  Register #(.width(5)) register_1 (.D(in), .Q(register_1_q), .clk(clock), .clr(reset));  // open: en
endmodule

module PipeReg4Ctrl (
  input  RegWrite,
  input  MemToReg,
  input  clock,
  input  reset,
  output RegWriteOut,
  output MemToRegOut
);

  Register #(.width(2)) register_1 (
    .D({MemToReg, RegWrite}), .Q({MemToRegOut, RegWriteOut}), .clk(clock), .clr(reset));  // open: en
endmodule

module PipeReg4DP (
  input  [31:0] ReadDataIn,
  input  [31:0] ALUOutIn,
  input  Clock,
  input  Reset,
  output [31:0] ReadDataOut,
  output [31:0] ALUOutOut
);

  Register #(.width(32)) register_1 (.D(ReadDataIn), .Q(ReadDataOut), .clk(Clock), .clr(Reset));  // open: en
  Register #(.width(32)) IR (.D(ALUOutIn), .Q(ALUOutOut), .clk(Clock), .clr(Reset));  // open: en
endmodule
