// Logisim project Latches.circ as structural Verilog: 2 circuits, main circuit DLatch
module DLatch (
  input  En,
  input  D,
  output Q
);

  wire and_1_out, and_2_out, nor_2_out, not_1_out;

  not not_1 (not_1_out, D);
  and and_1 (and_1_out, En, not_1_out);
  and and_2 (and_2_out, En, D);
  nor nor_1 (Q, and_1_out, nor_2_out);
  nor nor_2 (nor_2_out, Q, and_2_out);

  // Notes on the sheet:
  //   R
  //   S
endmodule

module SRLatch (
  input  R,
  input  S,
  output Q
);

  wire nor_2_out;

  nor nor_1 (Q, R, nor_2_out);
  nor nor_2 (nor_2_out, Q, S);
endmodule
