// Logisim project TrafficStartJF.circ as structural Verilog: 1 circuit, main circuit Traffic
module Traffic (
  input  BG,
  input  a,
  input  BCar,
  input  CCar,
  output BG2,
  output x
);

  wire and_1_out, and_2_out, and_3_out, and_4_out, and_5_out, and_6_out, not_1_out, not_2_out, not_3_out,
       not_4_out, not_5_out, not_6_out, not_7_out, not_8_out;

  not not_1 (not_1_out, CCar);
  not not_2 (not_2_out, BG);
  and and_1 (and_1_out, not_2_out, BCar);
  not not_3 (not_3_out, BG);
  and and_2 (and_2_out, not_3_out, a);
  and and_3 (and_3_out, BG, not_4_out);
  not not_4 (not_4_out, a);
  not not_5 (not_5_out, a);
  and and_4 (and_4_out, not_5_out, not_6_out, CCar);
  not not_6 (not_6_out, BCar);
  and and_5 (and_5_out, BG, not_7_out);
  not not_7 (not_7_out, a);
  and and_6 (and_6_out, BG, not_8_out);
  not not_8 (not_8_out, CCar);
  or or_1 (BG2, not_1_out, and_1_out, and_2_out, and_3_out);
  or or_2 (x, and_4_out, and_5_out, and_6_out);
endmodule
