// Logisim project trafficJF.circ as structural Verilog: 1 circuit, main circuit main
module main (
  input  BCar,
  input  CCar,
  output Reset_State_to_00
);

  wire clock_1_out;
  wire [1:0] StateRegister_q, transistion_bg2;

  Clock clock_1 (.out(clock_1_out));
  Register #(.width(2)) StateRegister (
    .D(transistion_bg2), .en(1'b1), .Q(StateRegister_q), .clk(clock_1_out), .clr(Reset_State_to_00));
  Traffic transistion (
    .BG(StateRegister_q[0]), .a(StateRegister_q[1]), .BCar(BCar), .CCar(CCar), .BG2(transistion_bg2[0]),
    .x(transistion_bg2[1]));
  LED Broad_Light (.in(StateRegister_q[0]));
endmodule
